# Fritzing sketch Test_water_sensor (saved by Fritzing 0.9.3b)
breadboards: 1

parts:
  Water_Level_Sensor = Water Level Sensor
  Componente1 = Arduino Uno (Rev3)
  LED1 = LED - 3mm [color="Red (633nm)" package="3 mm [THT]"]
  LED2 = LED - 3mm [color="Red (633nm)" package="3 mm [THT]"]
  LED3 = LED - 3mm [color="Red (633nm)" package="3 mm [THT]"]
  R1 = Resistor [tolerance=±5% resistance=220 package=THT]
  R2 = Resistor [tolerance=±5% resistance=220 package=THT]
  R3 = Resistor [tolerance=±5% resistance=220 package=THT]
  Q1 = NPN-Transistor [package="TO92 [THT]"]
  R4 = Resistor [tolerance=±5% resistance=220 package=THT]

nets:
  N1: Water_Level_Sensor.SIG, Componente1.A5/SCL
  VCC: Water_Level_Sensor.VCC, Componente1.5V
  N2: Water_Level_Sensor.GND, Q1.E
  N3: Componente1.D8, LED3.anode
  N4: Componente1.D9_PWM, LED2.cathode, R2.Pin_0
  N5: Componente1.D10_PWM/SS, LED1.cathode, R1.Pin_0
  N6: Componente1.GND, R2.Pin_1, R3.Pin_1, Q1.C
  N7: Componente1.D7, R4.Pin_0
  N8: LED3.cathode, R3.Pin_0
  N9: Q1.B, R4.Pin_1

custom parts:
  Water Level Sensor: A water level sensor. This sensor operates at 3V to 5V. The Sig (signal) pin outputs an analogue signal that is in proportion to the amount of water in contact with the sensor.
